// Logisim project A1_Group6.circ as structural Verilog: 2 circuits, main circuit main
module main (
  input  [2:0] S2,
  input  [3:0] A,
  input  [3:0] B,
  output [3:0] CF_OF_SF_ZF,
  output [3:0] Output
);

  wire adder_1_cout, adder_2_cout, adder_3_cout, adder_4_cout, and_1_out, and_2_out, and_3_out, and_4_out,
       and_5_out, and_6_out, and_7_out, and_8_out, and_9_out, not_1_out, not_2_out, not_3_out, not_4_out,
       not_5_out, not_6_out, or_1_out, or_2_out, or_3_out, or_4_out, or_5_out, or_6_out, or_7_out, or_8_out,
       or_9_out, or_10_out, or_11_out, xor_1_out, xor_2_out, xor_3_out, xor_4_out, xor_5_out;

  not not_1 (not_1_out, B[0]);
  not not_2 (not_2_out, B[1]);
  not not_3 (not_3_out, B[2]);
  not not_4 (not_4_out, B[3]);
  not not_5 (not_5_out, S2[1]);
  not not_6 (not_6_out, S2[0]);
  xor xor_1 (xor_1_out, S2[0], A[0]);
  and and_1 (and_1_out, S2[0], not_5_out);
  xor xor_2 (xor_2_out, S2[0], A[1]);
  xor xor_3 (xor_3_out, S2[0], A[2]);
  xor xor_4 (xor_4_out, S2[0], A[3]);
  and and_2 (and_2_out, and_1_out, not_1_out);
  and and_3 (and_3_out, and_1_out, not_2_out);
  and and_4 (and_4_out, and_1_out, not_3_out);
  and and_5 (and_5_out, and_1_out, not_4_out);
  or or_1 (or_1_out, xor_1_out, and_2_out);
  or or_2 (or_2_out, not_1_out, not_5_out);
  or or_3 (or_3_out, xor_2_out, and_3_out);
  or or_4 (or_4_out, not_2_out, not_5_out);
  or or_5 (or_5_out, xor_3_out, and_4_out);
  or or_6 (or_6_out, not_3_out, not_5_out);
  or or_7 (or_7_out, xor_4_out, and_5_out);
  or or_8 (or_8_out, not_4_out, not_5_out);
  and and_6 (and_6_out, S2[2], not_6_out);
  Adder #(.width(1)) adder_1 (.a(or_1_out), .b(or_2_out), .out(Output[0]), .cin(and_6_out), .cout(adder_1_cout));
  and and_7 (and_7_out, adder_1_cout, not_6_out);
  Adder #(.width(1)) adder_2 (.a(or_3_out), .b(or_4_out), .out(Output[1]), .cin(and_7_out), .cout(adder_2_cout));
  and and_8 (and_8_out, adder_2_cout, not_6_out);
  Adder #(.width(1)) adder_3 (.a(or_5_out), .b(or_6_out), .out(Output[2]), .cin(and_8_out), .cout(adder_3_cout));
  and and_9 (and_9_out, adder_3_cout, not_6_out);
  Adder #(.width(1)) adder_4 (.a(or_7_out), .b(or_8_out), .out(CF_OF_SF_ZF[1]), .cin(and_9_out), .cout(adder_4_cout));
  xor xor_5 (xor_5_out, and_9_out, adder_4_cout);
  or or_9 (or_9_out, Output[0], Output[1]);
  or or_10 (or_10_out, or_9_out, Output[2]);
  and and_10 (CF_OF_SF_ZF[2], xor_5_out, not_6_out);
  and and_11 (CF_OF_SF_ZF[3], adder_4_cout, not_6_out);
  or or_11 (or_11_out, or_10_out, CF_OF_SF_ZF[1]);
  not not_7 (CF_OF_SF_ZF[0], or_11_out);

  assign Output[3] = CF_OF_SF_ZF[1];

  // Notes on the sheet:
  //   Control bits
  //   S0
  //   S1
  //   c5
  //   SF
  //   OF
  //   CF
  //   ZF
  //   Status Flags
endmodule

module offline_1 (
  input  [2:0] cs2_cs1_cs0,
  input  [3:0] A,
  input  [3:0] B,
  output [3:0] cf_of_sf_zf,
  output [3:0] \output 
);

  main main_1 (.S2(cs2_cs1_cs0), .A(A), .B(B), .CF_OF_SF_ZF(cf_of_sf_zf), .Output(\output ));
endmodule
