// Logisim project A1_GROUP6.circ as structural Verilog: 8 circuits, main circuit main
module main (
  input  [15:0] input_A,
  input  [15:0] input_B,
  output [15:0] main_output,
  output overflow,
  output underflow
);

  wire adder_1_mux0, and_1_out, bitfinder_1_found, input_processing_1_sign_a_and_xor,
       input_processing_1_sign_b_and_xor, input_processing_1_xor_of_sign_bit, normalize_1_find_high_output;
  wire [3:0] adder_1_subresult, normalize_1_spliter_left;
  wire [15:0] adder_1_addresult, input_processing_1_significand_a, input_processing_1_significand_b,
       n2_s_complement_1_adder_final_out, normalize_1_normalize_output;

  Over_Under_flow over_under_flow_1 (
    .overflow(overflow), .underflow(underflow), .mux0(input_A[14:11]), .mux1(input_B[14:11]),
    .mux_select(adder_1_mux0), .spliterleft(normalize_1_spliter_left), .\and (normalize_1_find_high_output),
    .spliter_right(main_output[14:11]));
  Adder adder_1 (
    .sub1(input_A[14:11]), .sub2(input_B[14:11]), .Significand_A(input_processing_1_significand_a),
    .significand_B(input_processing_1_significand_b), .cin(input_processing_1_xor_of_sign_bit),
    .sign_A_and_xor(input_processing_1_sign_a_and_xor), .sign_B_and_xor(input_processing_1_sign_b_and_xor),
    .subresult(adder_1_subresult), .addresult(adder_1_addresult), .mux0(adder_1_mux0));
  Normalize normalize_1 (
    .Spliter_left(normalize_1_spliter_left), .find_high_output(normalize_1_find_high_output),
    .AdderOutput(n2_s_complement_1_adder_final_out),
    .Normalize_output({normalize_1_normalize_output[15:12], main_output[10:0], normalize_1_normalize_output[0]}));
  Input_processing input_processing_1 (
    .Fraction_of_A(input_A[10:0]), .Sign_of_A(input_A[15]), .Sign_of_B(input_B[15]),
    .Fraction_of_B(input_B[10:0]), .significand_A(input_processing_1_significand_a),
    .sign_A_and_xor(input_processing_1_sign_a_and_xor), .sign_B_and_xor(input_processing_1_sign_b_and_xor),
    .significand_B(input_processing_1_significand_b), .Xor_of_sign_bit(input_processing_1_xor_of_sign_bit));
  _2_s_complement u_2_s_complement_1 (
    .Adder_output(adder_1_addresult), .Adder_final_out(n2_s_complement_1_adder_final_out),
    .And_input(and_1_out));
  BitFinder #(.width(16), .\type ("high1")) bitfinder_1 (
    .in(adder_1_addresult), .found(bitfinder_1_found));  // open: index
  and and_1 (and_1_out, input_processing_1_xor_of_sign_bit, main_output[15]);
  sign sign_1 (
    .SignificandB(input_processing_1_significand_b), .subresult(adder_1_subresult), .SignBitOfB(input_B[15]),
    .XorOFSIgnBit(input_processing_1_xor_of_sign_bit), .SubCarry(adder_1_mux0), .FindHigh(bitfinder_1_found),
    .SignBitOfA(input_A[15]), .Sign(main_output[15]), .SignificandA(input_processing_1_significand_a));

  // Notes on the sheet:
  //   Overflow/ Underflow check
  //   Adder
  //   Normalize
  //   Input Processing
  //   Fraction
  //   2's complement
  //   sign bit
endmodule

module block (
  input  [15:0] A,
  input  [15:0] B,
  output [15:0] out_3,
  output UnderFlow,
  output OverFlow
);

  main main_1 (.input_A(A), .input_B(B), .overflow(OverFlow), .underflow(UnderFlow), .main_output(out_3));

  // Notes on the sheet:
  //   Floating Point Adder
  //   Result
endmodule

module Over_Under_flow (
  input  [3:0] mux0,
  input  [3:0] mux1,
  input  mux_select,
  input  [3:0] spliterleft,
  input  \and ,
  output [3:0] spliter_right,
  output overflow,
  output underflow
);

  wire and_1_out, comparator_1_gt, nor_1_out;
  wire [3:0] multiplexer_1_out;
  wire [4:0] adder_1_out;

  Multiplexer #(.width(4), .enable("false")) multiplexer_1 (
    .in0(mux0), .in1(mux1), .out(multiplexer_1_out), .sel(mux_select));
  Adder_part #(.width(5)) adder_1 (
    .a({1'b0, multiplexer_1_out}), .b({{2{spliterleft[3]}}, spliterleft[2:0]}), .out(adder_1_out), .cin(1'b0));  // open: cout
  Comparator #(.width(5), .mode("unsigned")) comparator_1 (
    .a(adder_1_out), .b(5'b01111), .gt(comparator_1_gt), .eq(overflow));  // open: lt
  or or_1 (underflow, comparator_1_gt, and_1_out);
  nor nor_1 (nor_1_out, adder_1_out[3], adder_1_out[2], adder_1_out[1], adder_1_out[0]);
  and and_1 (and_1_out, nor_1_out, \and );
  Multiplexer #(.width(4), .enable("false")) multiplexer_2 (
    .in0({4{\and }}), .in1(adder_1_out[3:0]), .out(spliter_right), .sel(\and ));

  // Notes on the sheet:
  //   overflow
  //   underflow
endmodule

module Adder (
  input  sign_A_and_xor,
  input  sign_B_and_xor,
  input  [15:0] Significand_A,
  input  [15:0] significand_B,
  input  [3:0] sub1,
  input  [3:0] sub2,
  input  cin,
  output [3:0] subresult,
  output [15:0] addresult,
  output mux0
);

  wire multiplexer_4_out, multiplexer_7_out;
  wire [3:0] multiplexer_1_out, negator_1_out;
  wire [15:0] multiplexer_2_out, multiplexer_3_out, multiplexer_5_out, multiplexer_6_out, negator_2_out,
       negator_3_out, shifter_1_out;

  Negator #(.width(4)) negator_1 (.in(subresult), .out(negator_1_out));
  Multiplexer #(.width(4), .enable("false")) multiplexer_1 (
    .in0(subresult), .in1(negator_1_out), .out(multiplexer_1_out), .sel(mux0));
  Multiplexer #(.width(16), .enable("false")) multiplexer_2 (
    .in0(significand_B), .in1(Significand_A), .out(multiplexer_2_out), .sel(mux0));
  Subtractor #(.width(4)) subtractor_1 (.a(sub1), .b(sub2), .out(subresult), .bin(1'b0), .bout(mux0));
  Shifter #(.width(16), .shift("lr")) shifter_1 (
    .in(multiplexer_2_out), .\dist (multiplexer_1_out), .out(shifter_1_out));
  Multiplexer #(.width(16), .enable("false")) multiplexer_3 (
    .in0(Significand_A), .in1(significand_B), .out(multiplexer_3_out), .sel(mux0));
  Negator #(.width(16)) negator_2 (.in(multiplexer_3_out), .out(negator_2_out));
  Negator #(.width(16)) negator_3 (.in(shifter_1_out), .out(negator_3_out));
  Multiplexer #(.enable("false")) multiplexer_4 (
    .in0(sign_B_and_xor), .in1(sign_A_and_xor), .out(multiplexer_4_out), .sel(mux0));
  Multiplexer #(.width(16), .enable("false")) multiplexer_5 (
    .in0(multiplexer_3_out), .in1(negator_2_out), .out(multiplexer_5_out), .sel(multiplexer_7_out));
  Multiplexer #(.width(16), .enable("false")) multiplexer_6 (
    .in0(shifter_1_out), .in1(negator_3_out), .out(multiplexer_6_out), .sel(multiplexer_4_out));
  Multiplexer #(.enable("false")) multiplexer_7 (
    .in0(sign_A_and_xor), .in1(sign_B_and_xor), .out(multiplexer_7_out), .sel(mux0));
  Adder_part #(.width(16)) adder_1 (
    .a(multiplexer_5_out), .b(multiplexer_6_out), .out(addresult), .cin(1'b0));  // open: cout
endmodule

// SignBit
module sign (
  input  [15:0] SignificandB,
  input  [15:0] SignificandA,
  input  SignBitOfA,
  input  [3:0] subresult,
  input  SignBitOfB,
  input  XorOFSIgnBit,
  input  SubCarry,
  input  FindHigh,
  output Sign
);

  wire comparator_1_gt, multiplexer_1_out, multiplexer_2_out, multiplexer_3_out, multiplexer_4_out, nor_1_out;

  Multiplexer #(.enable("false")) multiplexer_1 (
    .in0(SignBitOfB), .in1(multiplexer_3_out), .out(multiplexer_1_out), .sel(XorOFSIgnBit));
  and and_1 (Sign, FindHigh, multiplexer_1_out);
  nor nor_1 (nor_1_out, subresult[0], subresult[1], subresult[2], subresult[3]);
  Multiplexer #(.enable("false")) multiplexer_2 (
    .in0(SignBitOfA), .in1(SignBitOfB), .out(multiplexer_2_out), .sel(SubCarry));
  Multiplexer #(.enable("false")) multiplexer_3 (
    .in0(multiplexer_2_out), .in1(multiplexer_4_out), .out(multiplexer_3_out), .sel(nor_1_out));
  Comparator #(.width(16), .mode("unsigned")) comparator_1 (
    .a(SignificandA), .b(SignificandB), .gt(comparator_1_gt));  // open: eq, lt
  Multiplexer #(.enable("false")) multiplexer_4 (
    .in0(SignBitOfB), .in1(SignBitOfA), .out(multiplexer_4_out), .sel(comparator_1_gt));
endmodule

module Normalize (
  input  [15:0] AdderOutput,
  output [3:0] Spliter_left,
  output find_high_output,
  output [15:0] Normalize_output
);

  wire [3:0] and_1_out, and_2_out, and_3_out, bitfinder_1_index, not_1_out, subtractor_1_out;
  wire [3:3] subtractor_1_bout;
  wire [15:0] shifter_1_out;

  BitFinder #(.width(16), .\type ("high1")) bitfinder_1 (
    .in({2'b00, AdderOutput[13:0]}), .index(bitfinder_1_index), .found(find_high_output));
  Shifter #(.width(16)) shifter_1 (.in({2'b00, AdderOutput[13:0]}), .\dist (and_2_out), .out(shifter_1_out));
  Subtractor #(.width(4)) subtractor_1 (
    .a(4'b1100), .b(bitfinder_1_index), .out(subtractor_1_out), .bin(1'b0), .bout(subtractor_1_bout[3]));
  assign and_1_out = subtractor_1_out & {4{find_high_output}};  // AND_Gate and_1, 4 bits wide
  assign and_2_out = and_1_out & not_1_out;  // AND_Gate and_2, 4 bits wide
  assign not_1_out = ~{4{subtractor_1_bout[3]}};  // NOT_Gate not_1, 4 bits wide
  Negator #(.width(4)) negator_1 (.in(and_1_out), .out(Spliter_left));
  assign and_3_out = Spliter_left & {4{subtractor_1_bout[3]}};  // AND_Gate and_3, 4 bits wide
  Shifter #(.width(16), .shift("lr")) shifter_2 (.in(shifter_1_out), .\dist (and_3_out), .out(Normalize_output));
endmodule

module _2_s_complement (
  input  [15:0] Adder_output,
  input  And_input,
  output [15:0] Adder_final_out
);

  wire [15:0] negator_1_out;

  Multiplexer #(.width(16), .enable("false")) multiplexer_1 (
    .in0(Adder_output), .in1(negator_1_out), .out(Adder_final_out), .sel(And_input));
  Negator #(.width(16)) negator_1 (.in(Adder_output), .out(negator_1_out));
endmodule

module Input_processing (
  input  Sign_of_B,
  input  [10:0] Fraction_of_B,
  input  [10:0] Fraction_of_A,
  input  Sign_of_A,
  output sign_B_and_xor,
  output sign_A_and_xor,
  output Xor_of_sign_bit,
  output [15:0] significand_B,
  output [15:0] significand_A
);

  and and_1 (sign_A_and_xor, Sign_of_A, Xor_of_sign_bit);
  xor xor_1 (Xor_of_sign_bit, Sign_of_A, Sign_of_B);
  and and_2 (sign_B_and_xor, Xor_of_sign_bit, Sign_of_B);

  assign significand_A = {4'b0001, Fraction_of_A, 1'b0};
  assign significand_B = {4'b0001, Fraction_of_B, 1'b0};
endmodule
