// Logisim project 8_bits_MIPS_Processor_Group6.circ as structural Verilog: 6 circuits, main circuit main
module main (
  input  in_1,
  input  in_2,
  output [7:0] t2,
  output [7:0] t3,
  output [7:0] t1,
  output [7:0] t4,
  output [7:0] t0
);

  wire and_1_out, and_2_out, and_3_out, control_unit_1_alusrc, control_unit_1_branch, control_unit_1_jump,
       control_unit_1_memread, control_unit_1_memtoreg, control_unit_1_memwrite, control_unit_1_regdst,
       control_unit_1_regwrite, control_unit_1_shift, multiplexer_5_out, n8_bit_alu_1_zero_flag, nor_1_out,
       not_1_out;
  wire [2:0] control_unit_1_aluopcode;
  wire [3:0] instructions_memory_1_instruction_3_0, instructions_memory_1_instruction_11_8,
       instructions_memory_1_instructions__15_12, instructions_memory_1_opcode,
       instructions_memory_1_write_register;
  wire [7:0] adder_1_out, adder_2_out, data_memory_1_data_sor_write_reg,
       instructions_memory_1_instructions__7_0, instructions_memory_1_instructions__15_8,
       instructions_memory_1_pc_output, multiplexer_1_out, multiplexer_2_out, multiplexer_3_out,
       multiplexer_4_out, n8_bit_alu_1_output, register_file_1_output_reg_1, register_file_1_output_reg_2;

  Adder adder_1 (.a(instructions_memory_1_pc_output), .b(8'h1), .out(adder_1_out), .cin(1'b0));  // open: cout
  Instructions_memory instructions_memory_1 (
    .PC_input(multiplexer_1_out), .Instructions__7_0(instructions_memory_1_instructions__7_0),
    .Instructions__15_12(instructions_memory_1_instructions__15_12), .Reg_Destinition(control_unit_1_regdst),
    .Opcode(instructions_memory_1_opcode), .Instructions__15_8(instructions_memory_1_instructions__15_8),
    .PC_Output(instructions_memory_1_pc_output), .Write_Register(instructions_memory_1_write_register),
    .instruction_11_8(instructions_memory_1_instruction_11_8), .in_4(in_2),
    .Instruction_3_0(instructions_memory_1_instruction_3_0), .Reset(in_1));
  Multiplexer #(.width(8), .enable("false")) multiplexer_1 (
    .in0(multiplexer_4_out), .in1(instructions_memory_1_instructions__15_8), .out(multiplexer_1_out),
    .sel(control_unit_1_jump));
  Control_unit control_unit_1 (
    .Opcode(instructions_memory_1_opcode), .RegDst(control_unit_1_regdst), .Jump(control_unit_1_jump),
    .Branch(control_unit_1_branch), .MemRead(control_unit_1_memread), .MemToReg(control_unit_1_memtoreg),
    .ALUopcode(control_unit_1_aluopcode), .MemWrite(control_unit_1_memwrite), .ALUsrc(control_unit_1_alusrc),
    .RegWrite(control_unit_1_regwrite), .Shift(control_unit_1_shift));  // open: Control_output
  Register_file register_file_1 (
    .data_for_write_reg(data_memory_1_data_sor_write_reg), .Clock_pulse(in_2),
    .reg_write(control_unit_1_regwrite), .input_for_write_reg(instructions_memory_1_write_register),
    .Input_for_reg_1(instructions_memory_1_instructions__15_12),
    .Input_for_reg_2(instructions_memory_1_instruction_11_8), .output_reg_1(register_file_1_output_reg_1),
    .output_reg_2(register_file_1_output_reg_2), .t0(t0), .t1(t1), .t2(t2), .t3(t3), .t4(t4));  // open: sp, out_7
  Multiplexer #(.width(8), .enable("false")) multiplexer_2 (
    .in0(instructions_memory_1_instructions__7_0), .in1({4'b0000, instructions_memory_1_instruction_3_0}),
    .out(multiplexer_2_out), .sel(control_unit_1_shift));
  Multiplexer #(.width(8), .enable("false")) multiplexer_3 (
    .in0(register_file_1_output_reg_2), .in1(multiplexer_2_out), .out(multiplexer_3_out),
    .sel(control_unit_1_alusrc));
  Adder adder_2 (.a(adder_1_out), .b(multiplexer_2_out), .out(adder_2_out));  // open: cin, cout
  Multiplexer #(.width(8), .enable("false")) multiplexer_4 (
    .in0(adder_1_out), .in1(adder_2_out), .out(multiplexer_4_out), .sel(multiplexer_5_out));
  and and_1 (and_1_out, control_unit_1_branch, n8_bit_alu_1_zero_flag);
  _8_Bit_ALU u_8_bit_alu_1 (
    .Selector_Bit(control_unit_1_aluopcode), .A(register_file_1_output_reg_1), .B(multiplexer_3_out),
    .Output(n8_bit_alu_1_output), .Zero_flag(n8_bit_alu_1_zero_flag));
  not not_1 (not_1_out, n8_bit_alu_1_zero_flag);
  nor nor_1 (nor_1_out, instructions_memory_1_opcode[1], instructions_memory_1_opcode[2], instructions_memory_1_opcode[3]);
  Multiplexer #(.enable("false")) multiplexer_5 (
    .in0(and_1_out), .in1(and_3_out), .out(multiplexer_5_out), .sel(and_2_out));
  and and_2 (and_2_out, instructions_memory_1_opcode[0], nor_1_out);
  and and_3 (and_3_out, and_2_out, not_1_out);
  Data_memory data_memory_1 (
    .ALU_Output(n8_bit_alu_1_output), .Output_reg_2(register_file_1_output_reg_2),
    .Data_sor_write_reg(data_memory_1_data_sor_write_reg), .MemWrite(control_unit_1_memwrite),
    .MemRead(control_unit_1_memread), .MemToReg(control_unit_1_memtoreg), .Clock_Pulse(in_2));  // open: out_8
endmodule

module Control_unit (
  input  [3:0] Opcode,
  output [11:0] Control_output,
  output RegDst,
  output Jump,
  output Branch,
  output MemRead,
  output MemToReg,
  output [2:0] ALUopcode,
  output MemWrite,
  output ALUsrc,
  output RegWrite,
  output Shift
);

  ROM #(.addrWidth(4), .dataWidth(12)) rom_1 (
    .addr(Opcode),
    .data({Control_output[11], ALUsrc, Control_output[9:8], ALUopcode, Control_output[4:3], Branch, Control_output[1:0]}),
    .sel(1'b1));

  assign {Control_output[10], Control_output[7:5], Control_output[2]} = {ALUsrc, ALUopcode, Branch};
  assign Jump = Control_output[1];
  assign MemRead = Control_output[3];
  assign MemToReg = Control_output[4];
  assign MemWrite = Control_output[9];
  assign RegDst = Control_output[0];
  assign RegWrite = Control_output[11];
  assign Shift = Control_output[8];

  // Notes on the sheet:
  //   contents of rom_1 (hex, n*v repeats v):
  //   e2 24 c60 c18 c00 24 c20 861 821 801 841 da1 c40 881 600 dc1
  //   0-RegDst 1-Jump 2-Branch 3-MemRead 4-MemToReg 5,6,7,8-ALUopcode 9-MemWrite 10-ALUsrc 11-ReqWrite
endmodule

module Register_file (
  input  [7:0] data_for_write_reg,
  input  Clock_pulse,
  input  reg_write,
  input  [3:0] input_for_write_reg,
  input  [3:0] Input_for_reg_1,
  input  [3:0] Input_for_reg_2,
  output [7:0] out_7,
  output [7:0] sp,
  output [7:0] t0,
  output [7:0] t1,
  output [7:0] t2,
  output [7:0] t3,
  output [7:0] t4,
  output [7:0] output_reg_1,
  output [7:0] output_reg_2
);

  wire and_1_out, decoder_1_out0, decoder_1_out1, decoder_1_out2, decoder_1_out3, decoder_1_out4,
       decoder_1_out5, decoder_1_out6, decoder_1_out7;
  wire [2:0] multiplexer_1_out;
  wire [7:0] zero_reg_q;

  and and_1 (and_1_out, Clock_pulse, reg_write);
  Multiplexer #(.width(3), .enable("false")) multiplexer_1 (
    .in0(3'b000), .in1(input_for_write_reg[2:0]), .out(multiplexer_1_out), .sel(and_1_out));
  Decoder #(.select(3), .enable("false")) decoder_1 (
    .out0(decoder_1_out0), .out1(decoder_1_out1), .out2(decoder_1_out2), .out3(decoder_1_out3),
    .out4(decoder_1_out4), .out5(decoder_1_out5), .out6(decoder_1_out6), .out7(decoder_1_out7),
    .sel(multiplexer_1_out));
  Register zero_reg (.D({8{1'b0}}), .en(1'b1), .Q(zero_reg_q), .clk(decoder_1_out0));  // open: clr
  Register t0_reg (.D(data_for_write_reg), .en(1'b1), .Q(t0), .clk(decoder_1_out1));  // open: clr
  Register t1_reg (.D(data_for_write_reg), .en(1'b1), .Q(t1), .clk(decoder_1_out2));  // open: clr
  Register t2_reg (.D(data_for_write_reg), .en(1'b1), .Q(t2), .clk(decoder_1_out3));  // open: clr
  Register t3_reg (.D(data_for_write_reg), .en(1'b1), .Q(t3), .clk(decoder_1_out4));  // open: clr
  Register t4_reg (.D(data_for_write_reg), .en(1'b1), .Q(t4), .clk(decoder_1_out5));  // open: clr
  Register sp_reg (.D(data_for_write_reg), .en(1'b1), .Q(sp), .clk(decoder_1_out6));  // open: clr
  Register t5_reg (.D(data_for_write_reg), .en(1'b1), .Q(out_7), .clk(decoder_1_out7));  // open: clr
  Multiplexer #(.select(3), .width(8), .enable("false")) multiplexer_2 (
    .in0(zero_reg_q), .in1(t0), .in2(t1), .in3(t2), .in4(t3), .in5(t4), .in6(sp), .in7(out_7),
    .out(output_reg_1), .sel(Input_for_reg_1[2:0]));
  Multiplexer #(.select(3), .width(8), .enable("false")) multiplexer_3 (
    .in0(zero_reg_q), .in1(t0), .in2(t1), .in3(t2), .in4(t3), .in5(t4), .in6(sp), .in7(out_7),
    .out(output_reg_2), .sel(Input_for_reg_2[2:0]));

  // Notes on the sheet:
  //   t5
endmodule

module Data_memory (
  input  MemRead,
  input  MemWrite,
  input  MemToReg,
  input  [7:0] ALU_Output,
  input  [7:0] Output_reg_2,
  input  Clock_Pulse,
  output [7:0] Data_sor_write_reg,
  output [7:0] out_8
);

  RAM #(.bus("separate")) ram_1 (
    .addr(ALU_Output), .din(Output_reg_2), .data(out_8), .str(MemWrite), .clk(Clock_Pulse), .ld(MemRead));  // open: sel, clr
  Multiplexer #(.width(8), .enable("false")) multiplexer_1 (
    .in0(ALU_Output), .in1(out_8), .out(Data_sor_write_reg), .sel(MemToReg));
endmodule

module Instructions_memory (
  input  [7:0] PC_input,
  input  Reset,
  input  Reg_Destinition,
  input  in_4,
  output [7:0] PC_Output,
  output [3:0] Instruction_3_0,
  output [7:0] Instructions__7_0,
  output [3:0] instruction_11_8,
  output [3:0] Instructions__15_12,
  output [3:0] Opcode,
  output [3:0] Write_Register,
  output [7:0] Instructions__15_8
);

  Register #(.trigger("falling")) register_1 (.D(PC_input), .en(1'b1), .Q(PC_Output), .clk(in_4), .clr(Reset));
  ROM #(.dataWidth(20)) rom_1 (
    .addr(PC_Output),
    .data({Opcode, Instructions__15_8[7:4], instruction_11_8, Instructions__7_0[7:4], Instruction_3_0}));  // open: sel
  Multiplexer #(.width(4), .enable("false")) multiplexer_1 (
    .in0(instruction_11_8), .in1(Instructions__7_0[7:4]), .out(Write_Register), .sel(Reg_Destinition));

  assign Instructions__7_0[3:0] = Instruction_3_0;
  assign Instructions__15_8[3:0] = instruction_11_8;
  assign Instructions__15_12 = Instructions__15_8[7:4];

  // Notes on the sheet:
  //   contents of rom_1 (hex, n*v repeats v):
  //   406ff 40203 40304 92340 645fe 455ff b5051 85310 1700 f1021 92310 66601 e6100 43202 66601 35702 e6700
  //   22406 36100 46601 a4540 c4409 d4550 e5202 35302 93220 152ef
  //   Instructions [7-4]
  //   Instructions [11-8]
endmodule

module block_diagram (
  input  in_1,
  output [7:0] t0,
  output [7:0] t1,
  output [7:0] t2,
  output [7:0] t3,
  output [7:0] t4
);

  wire clock_1_out;

  Clock clock_1 (.out(clock_1_out));
  main main_1 (.t1(t1), .t2(t2), .t3(t3), .t0(t0), .t4(t4), .in_1(in_1), .in_2(clock_1_out));

  // Notes on the sheet:
  //   8 bits MIPS Processor
endmodule
