// Logisim project ALU_8_bits_group6.circ as structural Verilog: 2 circuits, main circuit main
module main (
);

  _8_Bit_ALU u_8_bit_alu_1 ();  // open: Selector_Bit, A, B, Output, Zero_flag
endmodule

module _8_Bit_ALU (
  input  [2:0] Selector_Bit,
  input  [7:0] A,
  input  [7:0] B,
  output [7:0] Output,
  output Zero_flag
);

  wire [7:0] adder_1_out, and_1_out, nor_1_out, or_1_out, shifter_1_out, shifter_2_out, subtractor_1_out;

  Adder adder_1 (.a(A), .b(B), .out(adder_1_out), .cin(1'b0));  // open: cout
  Subtractor subtractor_1 (.a(A), .b(B), .out(subtractor_1_out), .bin(1'b0));  // open: bout
  assign or_1_out = A | B;  // OR_Gate or_1, 8 bits wide
  assign and_1_out = A & B;  // AND_Gate and_1, 8 bits wide
  assign nor_1_out = ~(A | B);  // NOR_Gate nor_1, 8 bits wide
  Shifter shifter_1 (.in(A), .\dist (B[2:0]), .out(shifter_1_out));
  Shifter #(.shift("lr")) shifter_2 (.in(A), .\dist (B[2:0]), .out(shifter_2_out));
  Multiplexer #(.select(3), .width(8), .enable("false")) multiplexer_1 (
    .in0(adder_1_out), .in1(subtractor_1_out), .in2(or_1_out), .in3(and_1_out), .in4(nor_1_out),
    .in5(shifter_1_out), .in6(shifter_2_out), .in7({8{1'b0}}), .out(Output), .sel(Selector_Bit));
  nor nor_2 (Zero_flag, Output[0], Output[1], Output[2], Output[3], Output[4], Output[5], Output[6], Output[7]);
endmodule
