// Logisim project ALU_new.circ as structural Verilog: 2 circuits, main circuit main
module main (
);

  _8_Bit_ALU u_8_bit_alu_1 ();  // open: Selector_Bit, A, B, Output
endmodule

module _8_Bit_ALU (
  input  [1:0] Selector_Bit,
  input  [7:0] A,
  input  [7:0] B,
  output [7:0] Output
);

  wire [7:0] adder_1_out, and_1_out, or_1_out, subtractor_1_out;

  Adder adder_1 (.a(A), .b(B), .out(adder_1_out), .cin(1'b0));  // open: cout
  Subtractor subtractor_1 (.a(A), .b(B), .out(subtractor_1_out), .bin(1'b0));  // open: bout
  assign or_1_out = A | B;  // OR_Gate or_1, 8 bits wide
  assign and_1_out = A & B;  // AND_Gate and_1, 8 bits wide
  Multiplexer #(.select(2), .width(8), .enable("false")) multiplexer_1 (
    .in0(adder_1_out), .in1(subtractor_1_out), .in2(and_1_out), .in3(or_1_out), .out(Output),
    .sel(Selector_Bit));
endmodule
