// Logisim project Data Memory.circ as structural Verilog: 1 circuit, main circuit main
module main (
  input  MemRead,
  input  MemWrite,
  input  MemToReg,
  input  [7:0] ALU_Output,
  input  [7:0] Output_reg_2,
  input  Clock_Pulse,
  output [7:0] Data_for_write_reg,
  output [7:0] out_8
);

  RAM #(.bus("separate")) ram_1 (
    .addr(ALU_Output), .din(Output_reg_2), .data(out_8), .str(MemWrite), .clk(Clock_Pulse), .ld(MemRead));  // open: sel, clr
  Multiplexer #(.width(8), .enable("false")) multiplexer_1 (
    .in0(ALU_Output), .in1(out_8), .out(Data_for_write_reg), .sel(MemToReg));
endmodule
