// Logisim project MIPS.circ as structural Verilog: 9 circuits, main circuit main
module main (
  input  in_1,
  input  in_2,
  output [7:0] t4,
  output [7:0] t3,
  output [7:0] t2,
  output [7:0] t1,
  output [7:0] t0
);

  wire control_unit_1_regwrite, ex_mem_1_regwrite_bit, id_ex_1_regwrite_bit, mem_wb_1_regwrite_bit;
  wire [1:0] control_unit_1_aluopcode, id_ex_1_alu_opcode, main_1_forward_a, main_1_forward_b;
  wire [3:0] ex_mem_1_rd_2, id_ex_1_rd_2, id_ex_1_rs_2, id_ex_1_rt_2, if_id_1_ins_11_8_2,
       if_id_1_ins_15_12_2, if_id_1_opcode_19_16_2, if_id_1_write_reg_2,
       instruction_memory_1_instruction_11_8, instruction_memory_1_instructions__15_12,
       instruction_memory_1_opcode_19_16, instruction_memory_1_write_register, mem_wb_1_rd_2;
  wire [7:0] adder_1_out, ex_mem_1_alu_output, id_ex_1_output_reg_1_2, id_ex_1_output_reg_2,
       instruction_memory_1_pc_output, mem_wb_1_alu_output, multiplexer_1_out, multiplexer_2_out,
       n8_bit_alu_1_output, registers_1_output_reg_1, registers_1_output_reg_1_2;

  Instruction_Memory instruction_memory_1 (
    .PC_input(adder_1_out), .instruction_11_8(instruction_memory_1_instruction_11_8), .RESET(in_1),
    .Instructions__15_12(instruction_memory_1_instructions__15_12),
    .Opcode_19_16(instruction_memory_1_opcode_19_16), .PC_Output(instruction_memory_1_pc_output),
    .CLOCK(in_2), .Write_Register(instruction_memory_1_write_register));
  Adder adder_1 (.a(8'h1), .b(instruction_memory_1_pc_output), .out(adder_1_out), .cin(1'b0));  // open: cout
  IF_ID if_id_1 (
    .opcode_19_16(instruction_memory_1_opcode_19_16), .ins_15_12(instruction_memory_1_instructions__15_12),
    .ins_11_8(instruction_memory_1_instruction_11_8), .Write_Reg(instruction_memory_1_write_register),
    .CLK(in_2), .Reset(in_1), .Opcode_19_16_2(if_id_1_opcode_19_16_2), .Ins_15_12_2(if_id_1_ins_15_12_2),
    .Ins_11_8_2(if_id_1_ins_11_8_2), .Write_Reg_2(if_id_1_write_reg_2));
  Control_Unit control_unit_1 (
    .Opcode(if_id_1_opcode_19_16_2), .RegWrite(control_unit_1_regwrite), .ALUopcode(control_unit_1_aluopcode));  // open: Control_output
  registers registers_1 (
    .data_for_write_reg(mem_wb_1_alu_output), .Clock_pulse(in_2), .reg_write(mem_wb_1_regwrite_bit),
    .input_for_write_reg(mem_wb_1_rd_2), .Input_for_reg_1(if_id_1_ins_15_12_2),
    .Input_for_reg_2(if_id_1_ins_11_8_2), .output_reg_1(registers_1_output_reg_1),
    .output_reg_1_2(registers_1_output_reg_1_2), .t0(t0), .t1(t1), .t2(t2), .t3(t3), .t4(t4));
  ID_Ex id_ex_1 (
    .Reg_Write(control_unit_1_regwrite), .aluopcode(control_unit_1_aluopcode),
    .output_reg_1(registers_1_output_reg_1), .output_reg2(registers_1_output_reg_1_2),
    .rs(if_id_1_ins_15_12_2), .rt(if_id_1_ins_11_8_2), .rd(if_id_1_write_reg_2), .CLK(in_2), .Reset(in_1),
    .RegWrite_Bit(id_ex_1_regwrite_bit), .ALU_opcode(id_ex_1_alu_opcode),
    .Output_reg_1_2(id_ex_1_output_reg_1_2), .Output_reg_2(id_ex_1_output_reg_2), .rs_2(id_ex_1_rs_2),
    .rt_2(id_ex_1_rt_2), .rd_2(id_ex_1_rd_2));
  Multiplexer #(.select(2), .width(8), .enable("false")) multiplexer_1 (
    .in0(id_ex_1_output_reg_1_2), .in1(mem_wb_1_alu_output), .in2(ex_mem_1_alu_output),
    .out(multiplexer_1_out), .sel(main_1_forward_a));  // open: in3
  Multiplexer #(.select(2), .width(8), .enable("false")) multiplexer_2 (
    .in0(id_ex_1_output_reg_2), .in1(mem_wb_1_alu_output), .in2(ex_mem_1_alu_output),
    .out(multiplexer_2_out), .sel(main_1_forward_b));  // open: in3
  forwading_unit_main main_1 (
    .Ex_MemRegisterWrite(ex_mem_1_regwrite_bit), .ID_EX_RegisterRs(id_ex_1_rs_2),
    .ID_Ex_RegisterRt(id_ex_1_rt_2), .Ex_Mem_RegisterRd(ex_mem_1_rd_2), .Mem_WB_RegisterRd(mem_wb_1_rd_2),
    .Mem_WBRegisterWrite(mem_wb_1_regwrite_bit), .Forward_A(main_1_forward_a), .Forward_B(main_1_forward_b));
  _8_Bit_ALU u_8_bit_alu_1 (
    .Selector_Bit(id_ex_1_alu_opcode), .A(multiplexer_1_out), .B(multiplexer_2_out),
    .Output(n8_bit_alu_1_output));
  EX_MEM ex_mem_1 (
    .Reg_Write(id_ex_1_regwrite_bit), .ALU_ouput(n8_bit_alu_1_output), .rd(id_ex_1_rd_2), .CLK(in_2),
    .Reset(in_1), .RegWrite_Bit(ex_mem_1_regwrite_bit), .ALU_output(ex_mem_1_alu_output), .rd_2(ex_mem_1_rd_2));
  // Data_Memory_main main_2: pin names not known
  MEM_WB mem_wb_1 (
    .Reg_Write(ex_mem_1_regwrite_bit), .ALU_ouput(ex_mem_1_alu_output), .rd(ex_mem_1_rd_2), .CLK(in_2),
    .Reset(in_1), .RegWrite_Bit(mem_wb_1_regwrite_bit), .ALU_output(mem_wb_1_alu_output), .rd_2(mem_wb_1_rd_2));
endmodule

module IF_ID (
  input  [3:0] opcode_19_16,
  input  [3:0] ins_15_12,
  input  [3:0] ins_11_8,
  input  [3:0] Write_Reg,
  input  CLK,
  input  Reset,
  output [3:0] Opcode_19_16_2,
  output [3:0] Ins_15_12_2,
  output [3:0] Ins_11_8_2,
  output [3:0] Write_Reg_2
);

  Register #(.width(4)) register_1 (.D(opcode_19_16), .Q(Opcode_19_16_2), .clk(CLK), .clr(Reset));  // open: en
  Register #(.width(4)) register_2 (.D(ins_15_12), .Q(Ins_15_12_2), .clk(CLK), .clr(Reset));  // open: en
  Register #(.width(4)) register_3 (.D(ins_11_8), .Q(Ins_11_8_2), .clk(CLK), .clr(Reset));  // open: en
  Register #(.width(4)) register_4 (.D(Write_Reg), .Q(Write_Reg_2), .clk(CLK), .clr(Reset));  // open: en
endmodule

module ID_Ex (
  input  Reg_Write,
  input  [1:0] aluopcode,
  input  [7:0] output_reg_1,
  input  [7:0] output_reg2,
  input  [3:0] rs,
  input  [3:0] rt,
  input  [3:0] rd,
  input  CLK,
  input  Reset,
  output RegWrite_Bit,
  output [1:0] ALU_opcode,
  output [7:0] Output_reg_1_2,
  output [7:0] Output_reg_2,
  output [3:0] rs_2,
  output [3:0] rt_2,
  output [3:0] rd_2
);

  Register #(.width(1)) register_1 (.D(Reg_Write), .Q(RegWrite_Bit), .clk(CLK), .clr(Reset));  // open: en
  Register #(.width(2)) register_2 (.D(aluopcode), .Q(ALU_opcode), .clk(CLK), .clr(Reset));  // open: en
  Register register_3 (.D(output_reg_1), .Q(Output_reg_1_2), .clk(CLK), .clr(Reset));  // open: en
  Register register_4 (.D(output_reg2), .Q(Output_reg_2), .clk(CLK), .clr(Reset));  // open: en
  Register #(.width(4)) register_5 (.D(rs), .Q(rs_2), .clk(CLK), .clr(Reset));  // open: en
  Register #(.width(4)) register_6 (.D(rt), .Q(rt_2), .clk(CLK), .clr(Reset));  // open: en
  Register #(.width(4)) register_7 (.D(rd), .Q(rd_2), .clk(CLK), .clr(Reset));  // open: en

  // Notes on the sheet:
  //   Control ALU opcode
  //   Output reg 1
  //   Output reg 2
  //   RS
  //   RT
  //   Write Reg Rd
endmodule

module EX_MEM (
  input  Reg_Write,
  input  [7:0] ALU_ouput,
  input  [3:0] rd,
  input  CLK,
  input  Reset,
  output RegWrite_Bit,
  output [7:0] ALU_output,
  output [3:0] rd_2
);

  Register #(.width(1)) register_1 (.D(Reg_Write), .Q(RegWrite_Bit), .clk(CLK), .clr(Reset));  // open: en
  Register register_2 (.D(ALU_ouput), .Q(ALU_output), .clk(CLK), .clr(Reset));  // open: en
  Register #(.width(4)) register_3 (.D(rd), .Q(rd_2), .clk(CLK), .clr(Reset));  // open: en

  // Notes on the sheet:
  //   Write Reg Rd
endmodule

module MEM_WB (
  input  Reg_Write,
  input  [7:0] ALU_ouput,
  input  [3:0] rd,
  input  CLK,
  input  Reset,
  output RegWrite_Bit,
  output [7:0] ALU_output,
  output [3:0] rd_2
);

  Register #(.width(1)) register_1 (.D(Reg_Write), .Q(RegWrite_Bit), .clk(CLK), .clr(Reset));  // open: en
  Register register_2 (.D(ALU_ouput), .Q(ALU_output), .clk(CLK), .clr(Reset));  // open: en
  Register #(.width(4)) register_3 (.D(rd), .Q(rd_2), .clk(CLK), .clr(Reset));  // open: en

  // Notes on the sheet:
  //   Write Reg Rd
endmodule

module Instruction_Memory (
  input  [7:0] PC_input,
  input  RESET,
  input  CLOCK,
  output [7:0] PC_Output,
  output [3:0] instruction_11_8,
  output [3:0] Instructions__15_12,
  output [3:0] Opcode_19_16,
  output [3:0] Write_Register
);

  wire [3:0] rom_1_data;

  Register PC (.D(PC_input), .en(1'b1), .Q(PC_Output), .clk(CLOCK), .clr(RESET));
  ROM #(.dataWidth(20)) rom_1 (
    .addr(PC_Output), .data({Opcode_19_16, Instructions__15_12, instruction_11_8, Write_Register, rom_1_data}));  // open: sel

  // Notes on the sheet:
  //   contents of rom_1 (hex, n*v repeats v):
  //   2310 1420 12130 4540 22510 31250 3430 15210
  //   Instructions [7-4]
  //   Instructions [11-8]
endmodule

module Control_Unit (
  input  [3:0] Opcode,
  output [3:0] Control_output,
  output RegWrite,
  output [1:0] ALUopcode
);

  ROM #(.addrWidth(4), .dataWidth(4)) rom_1 (
    .addr(Opcode), .data({Control_output[3], ALUopcode, Control_output[0]}), .sel(1'b1));

  assign Control_output[2:1] = ALUopcode;
  assign RegWrite = Control_output[0];

  // Notes on the sheet:
  //   contents of rom_1 (hex, n*v repeats v):
  //   1 3 5 7
  //   0-RegWrite 1,2-ALUopcode
endmodule

module registers (
  input  [7:0] data_for_write_reg,
  input  Clock_pulse,
  input  reg_write,
  input  [3:0] input_for_write_reg,
  input  [3:0] Input_for_reg_1,
  input  [3:0] Input_for_reg_2,
  output [7:0] t4,
  output [7:0] t3,
  output [7:0] t2,
  output [7:0] t1,
  output [7:0] t0,
  output [7:0] output_reg_1,
  output [7:0] output_reg_1_2
);

  wire and_1_out, decoder_1_out0, decoder_1_out1, decoder_1_out2, decoder_1_out3, decoder_1_out4,
       decoder_1_out5, decoder_1_out6;
  wire [2:0] multiplexer_1_out;
  wire [7:0] sp_reg_q, zero_reg_q;

  and and_1 (and_1_out, Clock_pulse, reg_write);
  Multiplexer #(.width(3), .enable("false")) multiplexer_1 (
    .in0(3'b000), .in1(input_for_write_reg[2:0]), .out(multiplexer_1_out), .sel(and_1_out));
  Decoder #(.select(3), .enable("false")) decoder_1 (
    .out0(decoder_1_out0), .out1(decoder_1_out1), .out2(decoder_1_out2), .out3(decoder_1_out3),
    .out4(decoder_1_out4), .out5(decoder_1_out5), .out6(decoder_1_out6), .sel(multiplexer_1_out));  // open: out7
  Register zero_reg (.D({8{1'b0}}), .en(1'b1), .Q(zero_reg_q), .clk(decoder_1_out0));  // open: clr
  Register t0_reg (.D(data_for_write_reg), .en(1'b1), .Q(t0), .clk(decoder_1_out1));  // open: clr
  Register t1_reg (.D(data_for_write_reg), .en(1'b1), .Q(t1), .clk(decoder_1_out2));  // open: clr
  Register t2_reg (.D(data_for_write_reg), .en(1'b1), .Q(t2), .clk(decoder_1_out3));  // open: clr
  Register t3_reg (.D(data_for_write_reg), .en(1'b1), .Q(t3), .clk(decoder_1_out4));  // open: clr
  Register t4_reg (.D(data_for_write_reg), .en(1'b1), .Q(t4), .clk(decoder_1_out5));  // open: clr
  Register sp_reg (.D(data_for_write_reg), .en(1'b1), .Q(sp_reg_q), .clk(decoder_1_out6));  // open: clr
  Multiplexer #(.select(3), .width(8), .enable("false")) multiplexer_2 (
    .in0(zero_reg_q), .in1(t0), .in2(t1), .in3(t2), .in4(t3), .in5(t4), .in6(sp_reg_q), .out(output_reg_1),
    .sel(Input_for_reg_1[2:0]));  // open: in7
  Multiplexer #(.select(3), .width(8), .enable("false")) multiplexer_3 (
    .in0(zero_reg_q), .in1(t0), .in2(t1), .in3(t2), .in4(t3), .in5(t4), .in6(sp_reg_q), .out(output_reg_1_2),
    .sel(Input_for_reg_2[2:0]));  // open: in7
endmodule

module block_diagram (
  input  in_1,
  output [7:0] out_2,
  output [7:0] out_3,
  output [7:0] out_4,
  output [7:0] out_5,
  output [7:0] out_6
);

  wire clock_1_out;

  Clock clock_1 (.out(clock_1_out));
  main main_1 (.in_1(in_1), .t4(out_2), .t3(out_3), .t2(out_4), .t1(out_5), .t0(out_6), .in_2(clock_1_out));
endmodule
