// Logisim project forwading_unit.circ as structural Verilog: 2 circuits, main circuit main
module main (
  input  Ex_MemRegisterWrite,
  input  [3:0] ID_EX_RegisterRs,
  input  [3:0] ID_Ex_RegisterRt,
  input  [3:0] Ex_Mem_RegisterRd,
  input  [3:0] Mem_WB_RegisterRd,
  input  Mem_WBRegisterWrite,
  output [1:0] Forward_A,
  output [1:0] Forward_B
);

  wire and_1_out, and_2_out, and_3_out, and_4_out, and_5_out, and_6_out, and_7_out, and_8_out, nor_1_out,
       nor_2_out, nor_3_out, nor_4_out, not_1_out, not_2_out, or_1_out, or_2_out;
  wire [1:0] multiplexer_1_out, multiplexer_2_out, multiplexer_3_out, multiplexer_4_out;
  wire [3:0] xor_1_out, xor_2_out, xor_3_out, xor_4_out;

  or or_1 (or_1_out, Ex_Mem_RegisterRd[1], Ex_Mem_RegisterRd[0], Ex_Mem_RegisterRd[2], Ex_Mem_RegisterRd[3]);
  assign xor_1_out = ID_EX_RegisterRs ^ Ex_Mem_RegisterRd;  // XOR_Gate xor_1, 4 bits wide
  assign xor_2_out = ID_EX_RegisterRs ^ Mem_WB_RegisterRd;  // XOR_Gate xor_2, 4 bits wide
  assign xor_3_out = ID_Ex_RegisterRt ^ Ex_Mem_RegisterRd;  // XOR_Gate xor_3, 4 bits wide
  assign xor_4_out = ID_Ex_RegisterRt ^ Mem_WB_RegisterRd;  // XOR_Gate xor_4, 4 bits wide
  or or_2 (or_2_out, Mem_WB_RegisterRd[1], Mem_WB_RegisterRd[0], Mem_WB_RegisterRd[2], Mem_WB_RegisterRd[3]);
  and and_1 (and_1_out, or_1_out, Ex_MemRegisterWrite);
  nor nor_1 (nor_1_out, xor_1_out[0], xor_1_out[1], xor_1_out[2], xor_1_out[3]);
  nor nor_2 (nor_2_out, xor_2_out[1], xor_2_out[0], xor_2_out[2], xor_2_out[3]);
  nor nor_3 (nor_3_out, xor_3_out[1], xor_3_out[0], xor_3_out[2], xor_3_out[3]);
  nor nor_4 (nor_4_out, xor_4_out[1], xor_4_out[0], xor_4_out[2], xor_4_out[3]);
  and and_2 (and_2_out, or_2_out, Mem_WBRegisterWrite);
  and and_3 (and_3_out, and_1_out, nor_1_out);
  and and_4 (and_4_out, and_2_out, nor_2_out);
  and and_5 (and_5_out, nor_3_out, and_1_out);
  and and_6 (and_6_out, nor_4_out, and_2_out);
  not not_1 (not_1_out, and_3_out);
  not not_2 (not_2_out, and_5_out);
  Multiplexer #(.width(2), .enable("false")) multiplexer_1 (
    .in0(2'b00), .in1(2'b10), .out(multiplexer_1_out), .sel(and_3_out));
  Multiplexer #(.width(2), .enable("false")) multiplexer_2 (
    .in0(2'b00), .in1(2'b01), .out(multiplexer_2_out), .sel(and_7_out));
  and and_7 (and_7_out, not_1_out, and_4_out);
  Multiplexer #(.width(2), .enable("false")) multiplexer_3 (
    .in0(2'b00), .in1(2'b10), .out(multiplexer_3_out), .sel(and_5_out));
  Multiplexer #(.width(2), .enable("false")) multiplexer_4 (
    .in0(2'b00), .in1(2'b01), .out(multiplexer_4_out), .sel(and_8_out));
  and and_8 (and_8_out, not_2_out, and_6_out);
  Multiplexer #(.width(2), .enable("false")) multiplexer_5 (
    .in0(multiplexer_1_out), .in1(multiplexer_2_out), .out(Forward_A), .sel(and_7_out));
  Multiplexer #(.width(2), .enable("false")) multiplexer_6 (
    .in0(multiplexer_3_out), .in1(multiplexer_4_out), .out(Forward_B), .sel(and_8_out));

  // Notes on the sheet:
  //   ExMemRegRd!=0
  //   MemWBRegRd!=0
  //   Ex/Mem
  //   Ex Hazard FA
  //   Mem Hazard FA
  //   Ex Hazard FB
  //   Mem HAzard FB
  //   Mem/WB
endmodule

module block (
);

  main main_1 ();  // open: Ex_MemRegisterWrite, ID_EX_RegisterRs, ID_Ex_RegisterRt, Ex_Mem_RegisterRd, Mem_WB_RegisterRd, Mem_WBRegisterWrite, Forward_A, Forward_B
endmodule
